# Fritzing sketch LR1 (saved by Fritzing 1.0.2b)
breadboards: 1

parts:
  Part1 = Arduino Nano (Rev3.0)
  R5 = Resistor [tolerance=±5% resistance=330 power=0.25W package=THT]
  R6 = Resistor [tolerance=±5% resistance=10k power=0.25W package=THT]
  R7 = Resistor [tolerance=±5% resistance=10k power=0.25W package=THT]
  R8 = Resistor [tolerance=±5% resistance=10k power=0.25W package=THT]
  LED2 = LED - 5mm [color="Red (633nm)" current=0.030A package="5 mm [THT]"]
  S1 = Momentary Switch [package=ksa_sealed_tac_switch]
  S2 = Momentary Switch [package=ksa_sealed_tac_switch]
  S3 = Momentary Switch [package=ksa_sealed_tac_switch]

nets:
  N1: Part1.D1/TX, R6.Pin_0, S3.2, S3.4
  N2: Part1.RESET, LED2.cathode
  N3: Part1.D10, Part1.A1
  N4: Part1.A7, R6.Pin_1, R7.Pin_1, R8.Pin_1
  N5: R5.Pin_1, LED2.anode
  N6: R7.Pin_0, S2.2, S2.4
  N7: R8.Pin_0, S1.2, S1.4
  N8: S1.1, S1.3, S2.1, S2.3, S3.1, S3.3
