# Fritzing sketch LR1 (saved by Fritzing 0.9.5d)
breadboards: 1

parts:
  Компонент1 = Arduino Nano (Rev3.0)
  LED1 = LED - 5mm [color="Red (633nm)" package="5 mm [THT]"]
  R1 = Resistor [tolerance=±5% resistance=220 package=THT]

nets:
  N1: Компонент1.GND, LED1.cathode
  N2: Компонент1.A7, R1.Pin_0
  N3: LED1.anode, R1.Pin_1
